// Logisim project ALU_Design.circ as structural Verilog: 5 circuits, main circuit ALU32Bit
module ALU1Bit (
  input  [1:0] Operation,
  input  Ainvert,
  input  Binvert,
  input  CarryIn,
  input  A,
  input  B,
  input  Less,
  output Result,
  output CarryOut,
  output Set
);

  wire and_1_out, multiplexer_1_out, multiplexer_2_out, not_1_out, not_2_out, or_1_out;

  not not_1 (not_1_out, A);
  not not_2 (not_2_out, B);
  Multiplexer multiplexer_1 (.in0(A), .in1(not_1_out), .out(multiplexer_1_out), .sel(Ainvert));
  Multiplexer multiplexer_2 (.in0(B), .in1(not_2_out), .out(multiplexer_2_out), .sel(Binvert));
  and and_1 (and_1_out, multiplexer_1_out, multiplexer_2_out);
  or or_1 (or_1_out, multiplexer_1_out, multiplexer_2_out);
  Adder #(.width(1)) adder_1 (.a(multiplexer_1_out), .b(multiplexer_2_out), .out(Set), .cin(CarryIn), .cout(CarryOut));
  Multiplexer #(.select(2)) multiplexer_3 (
    .in0(and_1_out), .in1(or_1_out), .in2(Set), .in3(Less), .out(Result), .sel(Operation));
endmodule

module ALU32Bit (
  input  [31:0] A,
  input  Binvert,
  input  Ainvert,
  input  [31:0] B,
  input  [1:0] OP,
  output [31:0] Result,
  output Z,
  output N,
  output C,
  output V
);

  wire alu1bit_1_carryout, alu1bit_2_carryout, alu1bit_3_carryout, alu1bit_4_carryout, alu1bit_5_carryout,
       alu1bit_6_carryout, alu1bit_7_carryout, alu1bit_8_carryout, alu1bit_9_carryout, alu1bit_10_carryout,
       alu1bit_11_carryout, alu1bit_12_carryout, alu1bit_13_carryout, alu1bit_14_carryout,
       alu1bit_15_carryout, alu1bit_16_carryout, alu1bit_17_carryout, alu1bit_18_carryout,
       alu1bit_19_carryout, alu1bit_20_carryout, alu1bit_21_carryout, alu1bit_22_carryout,
       alu1bit_23_carryout, alu1bit_24_carryout, alu1bit_25_carryout, alu1bit_26_carryout,
       alu1bit_27_carryout, alu1bit_28_carryout, alu1bit_29_carryout, alu1bit_30_carryout,
       alu1bit_31_carryout, alu1bit_32_set, and_1_out, and_2_out, not_1_out, not_2_out, not_3_out, or_2_out;

  ALU1Bit alu1bit_1 (
    .Ainvert(Ainvert), .Less(alu1bit_32_set), .Binvert(Binvert), .CarryIn(Binvert), .Operation(OP), .A(A[0]),
    .B(B[0]), .CarryOut(alu1bit_1_carryout), .Result(Result[0]));  // open: Set
  ALU1Bit alu1bit_2 (
    .Ainvert(Ainvert), .Less(1'b0), .Binvert(Binvert), .CarryIn(alu1bit_1_carryout), .Operation(OP),
    .A(A[1]), .B(B[1]), .CarryOut(alu1bit_2_carryout), .Result(Result[1]));  // open: Set
  ALU1Bit alu1bit_3 (
    .Ainvert(Ainvert), .Less(1'b0), .Binvert(Binvert), .CarryIn(alu1bit_2_carryout), .Operation(OP),
    .A(A[2]), .B(B[2]), .CarryOut(alu1bit_3_carryout), .Result(Result[2]));  // open: Set
  ALU1Bit alu1bit_4 (
    .Ainvert(Ainvert), .Less(1'b0), .Binvert(Binvert), .CarryIn(alu1bit_3_carryout), .Operation(OP),
    .A(A[3]), .B(B[3]), .CarryOut(alu1bit_4_carryout), .Result(Result[3]));  // open: Set
  ALU1Bit alu1bit_5 (
    .Ainvert(Ainvert), .Less(1'b0), .Binvert(Binvert), .CarryIn(alu1bit_4_carryout), .Operation(OP),
    .A(A[4]), .B(B[4]), .CarryOut(alu1bit_5_carryout), .Result(Result[4]));  // open: Set
  ALU1Bit alu1bit_6 (
    .Ainvert(Ainvert), .Less(1'b0), .Binvert(Binvert), .CarryIn(alu1bit_5_carryout), .Operation(OP),
    .A(A[5]), .B(B[5]), .CarryOut(alu1bit_6_carryout), .Result(Result[5]));  // open: Set
  ALU1Bit alu1bit_7 (
    .Ainvert(Ainvert), .Less(1'b0), .Binvert(Binvert), .CarryIn(alu1bit_6_carryout), .Operation(OP),
    .A(A[6]), .B(B[6]), .CarryOut(alu1bit_7_carryout), .Result(Result[6]));  // open: Set
  ALU1Bit alu1bit_8 (
    .Ainvert(Ainvert), .Less(1'b0), .Binvert(Binvert), .CarryIn(alu1bit_7_carryout), .Operation(OP),
    .A(A[7]), .B(B[7]), .CarryOut(alu1bit_8_carryout), .Result(Result[7]));  // open: Set
  ALU1Bit alu1bit_9 (
    .Ainvert(Ainvert), .Less(1'b0), .Binvert(Binvert), .CarryIn(alu1bit_8_carryout), .Operation(OP),
    .A(A[8]), .B(B[8]), .CarryOut(alu1bit_9_carryout), .Result(Result[8]));  // open: Set
  ALU1Bit alu1bit_10 (
    .Ainvert(Ainvert), .Less(1'b0), .Binvert(Binvert), .CarryIn(alu1bit_9_carryout), .Operation(OP),
    .A(A[9]), .B(B[9]), .CarryOut(alu1bit_10_carryout), .Result(Result[9]));  // open: Set
  ALU1Bit alu1bit_11 (
    .Ainvert(Ainvert), .Less(1'b0), .Binvert(Binvert), .CarryIn(alu1bit_10_carryout), .Operation(OP),
    .A(A[10]), .B(B[10]), .CarryOut(alu1bit_11_carryout), .Result(Result[10]));  // open: Set
  ALU1Bit alu1bit_12 (
    .Ainvert(Ainvert), .Less(1'b0), .Binvert(Binvert), .CarryIn(alu1bit_11_carryout), .Operation(OP),
    .A(A[11]), .B(B[11]), .CarryOut(alu1bit_12_carryout), .Result(Result[11]));  // open: Set
  ALU1Bit alu1bit_13 (
    .Ainvert(Ainvert), .Less(1'b0), .Binvert(Binvert), .CarryIn(alu1bit_12_carryout), .Operation(OP),
    .A(A[12]), .B(B[12]), .CarryOut(alu1bit_13_carryout), .Result(Result[12]));  // open: Set
  ALU1Bit alu1bit_14 (
    .Ainvert(Ainvert), .Less(1'b0), .Binvert(Binvert), .CarryIn(alu1bit_13_carryout), .Operation(OP),
    .A(A[13]), .B(B[13]), .CarryOut(alu1bit_14_carryout), .Result(Result[13]));  // open: Set
  ALU1Bit alu1bit_15 (
    .Ainvert(Ainvert), .Less(1'b0), .Binvert(Binvert), .CarryIn(alu1bit_14_carryout), .Operation(OP),
    .A(A[14]), .B(B[14]), .CarryOut(alu1bit_15_carryout), .Result(Result[14]));  // open: Set
  ALU1Bit alu1bit_16 (
    .Ainvert(Ainvert), .Less(1'b0), .Binvert(Binvert), .CarryIn(alu1bit_15_carryout), .Operation(OP),
    .A(A[15]), .B(B[15]), .CarryOut(alu1bit_16_carryout), .Result(Result[15]));  // open: Set
  ALU1Bit alu1bit_17 (
    .Ainvert(Ainvert), .Less(1'b0), .Binvert(Binvert), .CarryIn(alu1bit_16_carryout), .Operation(OP),
    .A(A[16]), .B(B[16]), .CarryOut(alu1bit_17_carryout), .Result(Result[16]));  // open: Set
  ALU1Bit alu1bit_18 (
    .Ainvert(Ainvert), .Less(1'b0), .Binvert(Binvert), .CarryIn(alu1bit_17_carryout), .Operation(OP),
    .A(A[17]), .B(B[17]), .CarryOut(alu1bit_18_carryout), .Result(Result[17]));  // open: Set
  ALU1Bit alu1bit_19 (
    .Ainvert(Ainvert), .Less(1'b0), .Binvert(Binvert), .CarryIn(alu1bit_18_carryout), .Operation(OP),
    .A(A[18]), .B(B[18]), .CarryOut(alu1bit_19_carryout), .Result(Result[18]));  // open: Set
  ALU1Bit alu1bit_20 (
    .Ainvert(Ainvert), .Less(1'b0), .Binvert(Binvert), .CarryIn(alu1bit_19_carryout), .Operation(OP),
    .A(A[19]), .B(B[19]), .CarryOut(alu1bit_20_carryout), .Result(Result[19]));  // open: Set
  ALU1Bit alu1bit_21 (
    .Ainvert(Ainvert), .Less(1'b0), .Binvert(Binvert), .CarryIn(alu1bit_20_carryout), .Operation(OP),
    .A(A[20]), .B(B[20]), .CarryOut(alu1bit_21_carryout), .Result(Result[20]));  // open: Set
  ALU1Bit alu1bit_22 (
    .Ainvert(Ainvert), .Less(1'b0), .Binvert(Binvert), .CarryIn(alu1bit_21_carryout), .Operation(OP),
    .A(A[21]), .B(B[21]), .CarryOut(alu1bit_22_carryout), .Result(Result[21]));  // open: Set
  ALU1Bit alu1bit_23 (
    .Ainvert(Ainvert), .Less(1'b0), .Binvert(Binvert), .CarryIn(alu1bit_22_carryout), .Operation(OP),
    .A(A[22]), .B(B[22]), .CarryOut(alu1bit_23_carryout), .Result(Result[22]));  // open: Set
  ALU1Bit alu1bit_24 (
    .Ainvert(Ainvert), .Less(1'b0), .Binvert(Binvert), .CarryIn(alu1bit_23_carryout), .Operation(OP),
    .A(A[23]), .B(B[23]), .CarryOut(alu1bit_24_carryout), .Result(Result[23]));  // open: Set
  ALU1Bit alu1bit_25 (
    .Ainvert(Ainvert), .Less(1'b0), .Binvert(Binvert), .CarryIn(alu1bit_24_carryout), .Operation(OP),
    .A(A[24]), .B(B[24]), .CarryOut(alu1bit_25_carryout), .Result(Result[24]));  // open: Set
  ALU1Bit alu1bit_26 (
    .Ainvert(Ainvert), .Less(1'b0), .Binvert(Binvert), .CarryIn(alu1bit_25_carryout), .Operation(OP),
    .A(A[25]), .B(B[25]), .CarryOut(alu1bit_26_carryout), .Result(Result[25]));  // open: Set
  ALU1Bit alu1bit_27 (
    .Ainvert(Ainvert), .Less(1'b0), .Binvert(Binvert), .CarryIn(alu1bit_26_carryout), .Operation(OP),
    .A(A[26]), .B(B[26]), .CarryOut(alu1bit_27_carryout), .Result(Result[26]));  // open: Set
  ALU1Bit alu1bit_28 (
    .Ainvert(Ainvert), .Less(1'b0), .Binvert(Binvert), .CarryIn(alu1bit_27_carryout), .Operation(OP),
    .A(A[27]), .B(B[27]), .CarryOut(alu1bit_28_carryout), .Result(Result[27]));  // open: Set
  ALU1Bit alu1bit_29 (
    .Ainvert(Ainvert), .Less(1'b0), .Binvert(Binvert), .CarryIn(alu1bit_28_carryout), .Operation(OP),
    .A(A[28]), .B(B[28]), .CarryOut(alu1bit_29_carryout), .Result(Result[28]));  // open: Set
  ALU1Bit alu1bit_30 (
    .Ainvert(Ainvert), .Less(1'b0), .Binvert(Binvert), .CarryIn(alu1bit_29_carryout), .Operation(OP),
    .A(A[29]), .B(B[29]), .CarryOut(alu1bit_30_carryout), .Result(Result[29]));  // open: Set
  ALU1Bit alu1bit_31 (
    .Ainvert(Ainvert), .Less(1'b0), .Binvert(Binvert), .CarryIn(alu1bit_30_carryout), .Operation(OP),
    .A(A[30]), .B(B[30]), .CarryOut(alu1bit_31_carryout), .Result(Result[30]));  // open: Set
  ALU1Bit alu1bit_32 (
    .Ainvert(Ainvert), .Less(1'b0), .Binvert(Binvert), .CarryIn(alu1bit_31_carryout), .Operation(OP),
    .A(A[31]), .B(B[31]), .CarryOut(C), .Set(alu1bit_32_set), .Result(N));
  not not_1 (not_1_out, A[31]);
  not not_2 (not_2_out, B[31]);
  not not_3 (not_3_out, alu1bit_31_carryout);
  and and_1 (and_1_out, alu1bit_31_carryout, not_1_out, not_2_out);
  and and_2 (and_2_out, not_3_out, A[31], B[31]);
  or or_1 (V, and_1_out, and_2_out);
  or or_2 (or_2_out, Result[0], Result[1], Result[2], Result[3], Result[4], Result[5], Result[6], Result[7], Result[8], Result[9], Result[10], Result[11], Result[12], Result[13], Result[14], Result[15], Result[16], Result[17], Result[18], Result[19], Result[20], Result[21], Result[22], Result[23], Result[24], Result[25], Result[26], Result[27], Result[28], Result[29], Result[30], N, 1'b0);
  not not_4 (Z, or_2_out);

  assign Result[31] = N;
endmodule

module temp (
  input  [3:0] ALUOp,
  input  A,
  input  B,
  input  Less,
  output Result,
  output C,
  output Set
);

  ALU1Bit alu1bit_1 (
    .Ainvert(ALUOp[3]), .Less(Less), .Binvert(ALUOp[2]), .CarryIn(ALUOp[2]), .Operation(ALUOp[1:0]), .A(A),
    .B(B), .CarryOut(C), .Set(Set), .Result(Result));
endmodule

module temp_top (
  input  [3:0] in_1,
  input  in_2,
  input  in_3,
  input  in_4,
  output out_5
);

  temp temp_1 (.ALUOp(in_1), .A(in_2), .B(in_3), .Less(in_4), .Result(out_5));  // open: C, Set
endmodule

module ALU32BitTester (
  input  [31:0] in_1,
  input  in_2,
  input  in_3,
  input  [1:0] in_4,
  input  [31:0] in_5,
  output [31:0] out_6,
  output out_7,
  output out_8,
  output out_9,
  output out_10
);

  ALU32Bit alu32bit_1 (
    .Ainvert(in_3), .Binvert(in_2), .OP(in_4), .B(in_5), .A(in_1), .Result(out_6), .N(out_8), .C(out_9),
    .V(out_10), .Z(out_7));
endmodule
