// Logisim project AllInOneProcessor.circ as structural Verilog: 14 circuits, main circuit main
module main (
  input  Clock,
  input  [31:0] in_2,
  output [31:0] out_3,
  output out_4,
  output out_5,
  output out_6
);

  wire alu32bit_1_z, alucontrol_1_alucont2, alucontrol_1_alucont3, and_1_out, controlunit_1_aluop1,
       controlunit_1_aluop2, controlunit_1_alusrc, controlunit_1_branch, controlunit_1_jump,
       controlunit_1_memread, controlunit_1_memtoreg, controlunit_1_memwrite, controlunit_1_regdest,
       controlunit_1_regwrite;
  wire [1:0] alucontrol_1_alucont0;
  wire [3:0] pcpath_1_sum, pcpath_1_sum_2, pcpath_1_sum_3, pcpath_1_sum_4, pcpath_1_sum_5, pcpath_1_sum_6,
       pcpath_1_sum_7;
  wire [4:0] multiplexer_1_out;
  wire [15:0] alu32bit_1_result, alu32bit_1_result_2;
  wire [27:0] bit_extender_1_out, multiplier_1_out;
  wire [31:0] adder_1_out, bit_extender_2_out, multiplexer_2_out, multiplexer_3_out, multiplexer_4_out,
       multiplexer_5_out, multiplier_2_out, ram_1_dout, registergroup_1_readdata1, registergroup_1_readdata2;
  wire [31:28] pcpath_1_sum_8;

  PCPath pcpath_1 (
    .D(multiplexer_4_out), .in_2(Clock),
    .SUM({pcpath_1_sum_8, pcpath_1_sum_7, pcpath_1_sum_6, pcpath_1_sum_5, pcpath_1_sum_4, pcpath_1_sum_3, pcpath_1_sum_2, pcpath_1_sum}),
    .ReadAddress(out_3));
  Multiplexer #(.width(5)) multiplexer_1 (
    .in0(in_2[20:16]), .in1(in_2[15:11]), .out(multiplexer_1_out), .sel(controlunit_1_regdest));
  assign bit_extender_1_out = {{2{in_2[25]}}, in_2[25:0]};  // Bit_Extender bit_extender_1
  Multiplier #(.width(28)) multiplier_1 (.a(bit_extender_1_out), .b(28'h4), .out(multiplier_1_out));  // open: cin, cout
  assign bit_extender_2_out = {{16{in_2[15]}}, in_2[15:0]};  // Bit_Extender bit_extender_2
  ControlUnit controlunit_1 (
    .in_1(in_2[31:26]), .RegDest(controlunit_1_regdest), .ALUSrc(controlunit_1_alusrc),
    .MemtoReg(controlunit_1_memtoreg), .RegWrite(controlunit_1_regwrite), .MemRead(controlunit_1_memread),
    .MemWrite(controlunit_1_memwrite), .Branch(controlunit_1_branch), .ALUOp1(controlunit_1_aluop1),
    .ALUOp2(controlunit_1_aluop2), .Jump(controlunit_1_jump));
  RegisterGroup registergroup_1 (
    .RegWrite(controlunit_1_regwrite), .CLK(Clock), .ReadReg1(in_2[25:21]), .WriteReg(multiplexer_1_out),
    .ReadReg2(in_2[20:16]), .WriteData(multiplexer_5_out), .ReadData1(registergroup_1_readdata1),
    .ReadData2(registergroup_1_readdata2));
  ALUControl alucontrol_1 (
    .ALUOp1(controlunit_1_aluop1), .ALUOp0(controlunit_1_aluop2), .Funct0(in_2[0]), .Funct1(in_2[1]),
    .Funct2(in_2[2]), .Funct3(in_2[3]), .Funct4(in_2[4]), .Funct5(in_2[5]),
    .ALUCont0(alucontrol_1_alucont0[0]), .ALUCont1(alucontrol_1_alucont0[1]),
    .ALUCont2(alucontrol_1_alucont2), .ALUCont3(alucontrol_1_alucont3));
  Multiplexer #(.width(32)) multiplexer_2 (
    .in0(registergroup_1_readdata2), .in1(bit_extender_2_out), .out(multiplexer_2_out),
    .sel(controlunit_1_alusrc));
  Multiplier #(.width(32)) multiplier_2 (.a(bit_extender_2_out), .b(32'h4), .out(multiplier_2_out));  // open: cin, cout
  ALU32Bit alu32bit_1 (
    .Ainvert(alucontrol_1_alucont3), .Binvert(alucontrol_1_alucont2), .OP(alucontrol_1_alucont0),
    .B(multiplexer_2_out), .A(registergroup_1_readdata1), .Result({alu32bit_1_result_2, alu32bit_1_result}),
    .N(out_4), .C(out_5), .V(out_6), .Z(alu32bit_1_z));
  Adder #(.width(32)) adder_1 (
    .a({pcpath_1_sum_8, pcpath_1_sum_7, pcpath_1_sum_6, pcpath_1_sum_5, pcpath_1_sum_4, pcpath_1_sum_3, pcpath_1_sum_2, pcpath_1_sum}),
    .b(multiplier_2_out), .out(adder_1_out));  // open: cin, cout
  RAM #(.addrWidth(16), .dataWidth(32)) ram_1 (
    .addr(alu32bit_1_result), .we(controlunit_1_memwrite), .oe(controlunit_1_memread), .clk(Clock),
    .din(registergroup_1_readdata2), .dout(ram_1_dout));
  Multiplexer #(.width(32)) multiplexer_3 (
    .in0({pcpath_1_sum_8, pcpath_1_sum_7, pcpath_1_sum_6, pcpath_1_sum_5, pcpath_1_sum_4, pcpath_1_sum_3, pcpath_1_sum_2, pcpath_1_sum}),
    .in1(adder_1_out), .out(multiplexer_3_out), .sel(and_1_out));
  Multiplexer #(.width(32)) multiplexer_4 (
    .in0(multiplexer_3_out), .in1({pcpath_1_sum_8, multiplier_1_out}), .out(multiplexer_4_out),
    .sel(controlunit_1_jump));
  and and_1 (and_1_out, controlunit_1_branch, alu32bit_1_z);
  Multiplexer #(.width(32)) multiplexer_5 (
    .in0({alu32bit_1_result_2, alu32bit_1_result}), .in1(ram_1_dout), .out(multiplexer_5_out),
    .sel(controlunit_1_memtoreg));
endmodule

module ALU1Bit (
  input  [1:0] Operation,
  input  Ainvert,
  input  Binvert,
  input  CarryIn,
  input  A,
  input  B,
  input  Less,
  output Result,
  output CarryOut,
  output Set
);

  wire and_1_out, multiplexer_1_out, multiplexer_2_out, not_1_out, not_2_out, or_1_out;

  not not_1 (not_1_out, A);
  not not_2 (not_2_out, B);
  Multiplexer multiplexer_1 (.in0(A), .in1(not_1_out), .out(multiplexer_1_out), .sel(Ainvert));
  Multiplexer multiplexer_2 (.in0(B), .in1(not_2_out), .out(multiplexer_2_out), .sel(Binvert));
  and and_1 (and_1_out, multiplexer_1_out, multiplexer_2_out);
  or or_1 (or_1_out, multiplexer_1_out, multiplexer_2_out);
  Adder #(.width(1)) adder_1 (.a(multiplexer_1_out), .b(multiplexer_2_out), .out(Set), .cin(CarryIn), .cout(CarryOut));
  Multiplexer #(.select(2)) multiplexer_3 (
    .in0(and_1_out), .in1(or_1_out), .in2(Set), .in3(Less), .out(Result), .sel(Operation));
endmodule

module ALU32Bit (
  input  [31:0] A,
  input  Binvert,
  input  Ainvert,
  input  [31:0] B,
  input  [1:0] OP,
  output [31:0] Result,
  output Z,
  output N,
  output C,
  output V
);

  wire alu1bit_1_carryout, alu1bit_2_carryout, alu1bit_3_carryout, alu1bit_4_carryout, alu1bit_5_carryout,
       alu1bit_6_carryout, alu1bit_7_carryout, alu1bit_8_carryout, alu1bit_9_carryout, alu1bit_10_carryout,
       alu1bit_11_carryout, alu1bit_12_carryout, alu1bit_13_carryout, alu1bit_14_carryout,
       alu1bit_15_carryout, alu1bit_16_carryout, alu1bit_17_carryout, alu1bit_18_carryout,
       alu1bit_19_carryout, alu1bit_20_carryout, alu1bit_21_carryout, alu1bit_22_carryout,
       alu1bit_23_carryout, alu1bit_24_carryout, alu1bit_25_carryout, alu1bit_26_carryout,
       alu1bit_27_carryout, alu1bit_28_carryout, alu1bit_29_carryout, alu1bit_30_carryout,
       alu1bit_31_carryout, alu1bit_32_set, and_1_out, and_2_out, not_1_out, not_2_out, not_3_out, or_2_out;

  ALU1Bit alu1bit_1 (
    .Ainvert(Ainvert), .Less(alu1bit_32_set), .Binvert(Binvert), .CarryIn(Binvert), .Operation(OP), .A(A[0]),
    .B(B[0]), .CarryOut(alu1bit_1_carryout), .Result(Result[0]));  // open: Set
  ALU1Bit alu1bit_2 (
    .Ainvert(Ainvert), .Less(1'b0), .Binvert(Binvert), .CarryIn(alu1bit_1_carryout), .Operation(OP),
    .A(A[1]), .B(B[1]), .CarryOut(alu1bit_2_carryout), .Result(Result[1]));  // open: Set
  ALU1Bit alu1bit_3 (
    .Ainvert(Ainvert), .Less(1'b0), .Binvert(Binvert), .CarryIn(alu1bit_2_carryout), .Operation(OP),
    .A(A[2]), .B(B[2]), .CarryOut(alu1bit_3_carryout), .Result(Result[2]));  // open: Set
  ALU1Bit alu1bit_4 (
    .Ainvert(Ainvert), .Less(1'b0), .Binvert(Binvert), .CarryIn(alu1bit_3_carryout), .Operation(OP),
    .A(A[3]), .B(B[3]), .CarryOut(alu1bit_4_carryout), .Result(Result[3]));  // open: Set
  ALU1Bit alu1bit_5 (
    .Ainvert(Ainvert), .Less(1'b0), .Binvert(Binvert), .CarryIn(alu1bit_4_carryout), .Operation(OP),
    .A(A[4]), .B(B[4]), .CarryOut(alu1bit_5_carryout), .Result(Result[4]));  // open: Set
  ALU1Bit alu1bit_6 (
    .Ainvert(Ainvert), .Less(1'b0), .Binvert(Binvert), .CarryIn(alu1bit_5_carryout), .Operation(OP),
    .A(A[5]), .B(B[5]), .CarryOut(alu1bit_6_carryout), .Result(Result[5]));  // open: Set
  ALU1Bit alu1bit_7 (
    .Ainvert(Ainvert), .Less(1'b0), .Binvert(Binvert), .CarryIn(alu1bit_6_carryout), .Operation(OP),
    .A(A[6]), .B(B[6]), .CarryOut(alu1bit_7_carryout), .Result(Result[6]));  // open: Set
  ALU1Bit alu1bit_8 (
    .Ainvert(Ainvert), .Less(1'b0), .Binvert(Binvert), .CarryIn(alu1bit_7_carryout), .Operation(OP),
    .A(A[7]), .B(B[7]), .CarryOut(alu1bit_8_carryout), .Result(Result[7]));  // open: Set
  ALU1Bit alu1bit_9 (
    .Ainvert(Ainvert), .Less(1'b0), .Binvert(Binvert), .CarryIn(alu1bit_8_carryout), .Operation(OP),
    .A(A[8]), .B(B[8]), .CarryOut(alu1bit_9_carryout), .Result(Result[8]));  // open: Set
  ALU1Bit alu1bit_10 (
    .Ainvert(Ainvert), .Less(1'b0), .Binvert(Binvert), .CarryIn(alu1bit_9_carryout), .Operation(OP),
    .A(A[9]), .B(B[9]), .CarryOut(alu1bit_10_carryout), .Result(Result[9]));  // open: Set
  ALU1Bit alu1bit_11 (
    .Ainvert(Ainvert), .Less(1'b0), .Binvert(Binvert), .CarryIn(alu1bit_10_carryout), .Operation(OP),
    .A(A[10]), .B(B[10]), .CarryOut(alu1bit_11_carryout), .Result(Result[10]));  // open: Set
  ALU1Bit alu1bit_12 (
    .Ainvert(Ainvert), .Less(1'b0), .Binvert(Binvert), .CarryIn(alu1bit_11_carryout), .Operation(OP),
    .A(A[11]), .B(B[11]), .CarryOut(alu1bit_12_carryout), .Result(Result[11]));  // open: Set
  ALU1Bit alu1bit_13 (
    .Ainvert(Ainvert), .Less(1'b0), .Binvert(Binvert), .CarryIn(alu1bit_12_carryout), .Operation(OP),
    .A(A[12]), .B(B[12]), .CarryOut(alu1bit_13_carryout), .Result(Result[12]));  // open: Set
  ALU1Bit alu1bit_14 (
    .Ainvert(Ainvert), .Less(1'b0), .Binvert(Binvert), .CarryIn(alu1bit_13_carryout), .Operation(OP),
    .A(A[13]), .B(B[13]), .CarryOut(alu1bit_14_carryout), .Result(Result[13]));  // open: Set
  ALU1Bit alu1bit_15 (
    .Ainvert(Ainvert), .Less(1'b0), .Binvert(Binvert), .CarryIn(alu1bit_14_carryout), .Operation(OP),
    .A(A[14]), .B(B[14]), .CarryOut(alu1bit_15_carryout), .Result(Result[14]));  // open: Set
  ALU1Bit alu1bit_16 (
    .Ainvert(Ainvert), .Less(1'b0), .Binvert(Binvert), .CarryIn(alu1bit_15_carryout), .Operation(OP),
    .A(A[15]), .B(B[15]), .CarryOut(alu1bit_16_carryout), .Result(Result[15]));  // open: Set
  ALU1Bit alu1bit_17 (
    .Ainvert(Ainvert), .Less(1'b0), .Binvert(Binvert), .CarryIn(alu1bit_16_carryout), .Operation(OP),
    .A(A[16]), .B(B[16]), .CarryOut(alu1bit_17_carryout), .Result(Result[16]));  // open: Set
  ALU1Bit alu1bit_18 (
    .Ainvert(Ainvert), .Less(1'b0), .Binvert(Binvert), .CarryIn(alu1bit_17_carryout), .Operation(OP),
    .A(A[17]), .B(B[17]), .CarryOut(alu1bit_18_carryout), .Result(Result[17]));  // open: Set
  ALU1Bit alu1bit_19 (
    .Ainvert(Ainvert), .Less(1'b0), .Binvert(Binvert), .CarryIn(alu1bit_18_carryout), .Operation(OP),
    .A(A[18]), .B(B[18]), .CarryOut(alu1bit_19_carryout), .Result(Result[18]));  // open: Set
  ALU1Bit alu1bit_20 (
    .Ainvert(Ainvert), .Less(1'b0), .Binvert(Binvert), .CarryIn(alu1bit_19_carryout), .Operation(OP),
    .A(A[19]), .B(B[19]), .CarryOut(alu1bit_20_carryout), .Result(Result[19]));  // open: Set
  ALU1Bit alu1bit_21 (
    .Ainvert(Ainvert), .Less(1'b0), .Binvert(Binvert), .CarryIn(alu1bit_20_carryout), .Operation(OP),
    .A(A[20]), .B(B[20]), .CarryOut(alu1bit_21_carryout), .Result(Result[20]));  // open: Set
  ALU1Bit alu1bit_22 (
    .Ainvert(Ainvert), .Less(1'b0), .Binvert(Binvert), .CarryIn(alu1bit_21_carryout), .Operation(OP),
    .A(A[21]), .B(B[21]), .CarryOut(alu1bit_22_carryout), .Result(Result[21]));  // open: Set
  ALU1Bit alu1bit_23 (
    .Ainvert(Ainvert), .Less(1'b0), .Binvert(Binvert), .CarryIn(alu1bit_22_carryout), .Operation(OP),
    .A(A[22]), .B(B[22]), .CarryOut(alu1bit_23_carryout), .Result(Result[22]));  // open: Set
  ALU1Bit alu1bit_24 (
    .Ainvert(Ainvert), .Less(1'b0), .Binvert(Binvert), .CarryIn(alu1bit_23_carryout), .Operation(OP),
    .A(A[23]), .B(B[23]), .CarryOut(alu1bit_24_carryout), .Result(Result[23]));  // open: Set
  ALU1Bit alu1bit_25 (
    .Ainvert(Ainvert), .Less(1'b0), .Binvert(Binvert), .CarryIn(alu1bit_24_carryout), .Operation(OP),
    .A(A[24]), .B(B[24]), .CarryOut(alu1bit_25_carryout), .Result(Result[24]));  // open: Set
  ALU1Bit alu1bit_26 (
    .Ainvert(Ainvert), .Less(1'b0), .Binvert(Binvert), .CarryIn(alu1bit_25_carryout), .Operation(OP),
    .A(A[25]), .B(B[25]), .CarryOut(alu1bit_26_carryout), .Result(Result[25]));  // open: Set
  ALU1Bit alu1bit_27 (
    .Ainvert(Ainvert), .Less(1'b0), .Binvert(Binvert), .CarryIn(alu1bit_26_carryout), .Operation(OP),
    .A(A[26]), .B(B[26]), .CarryOut(alu1bit_27_carryout), .Result(Result[26]));  // open: Set
  ALU1Bit alu1bit_28 (
    .Ainvert(Ainvert), .Less(1'b0), .Binvert(Binvert), .CarryIn(alu1bit_27_carryout), .Operation(OP),
    .A(A[27]), .B(B[27]), .CarryOut(alu1bit_28_carryout), .Result(Result[27]));  // open: Set
  ALU1Bit alu1bit_29 (
    .Ainvert(Ainvert), .Less(1'b0), .Binvert(Binvert), .CarryIn(alu1bit_28_carryout), .Operation(OP),
    .A(A[28]), .B(B[28]), .CarryOut(alu1bit_29_carryout), .Result(Result[28]));  // open: Set
  ALU1Bit alu1bit_30 (
    .Ainvert(Ainvert), .Less(1'b0), .Binvert(Binvert), .CarryIn(alu1bit_29_carryout), .Operation(OP),
    .A(A[29]), .B(B[29]), .CarryOut(alu1bit_30_carryout), .Result(Result[29]));  // open: Set
  ALU1Bit alu1bit_31 (
    .Ainvert(Ainvert), .Less(1'b0), .Binvert(Binvert), .CarryIn(alu1bit_30_carryout), .Operation(OP),
    .A(A[30]), .B(B[30]), .CarryOut(alu1bit_31_carryout), .Result(Result[30]));  // open: Set
  ALU1Bit alu1bit_32 (
    .Ainvert(Ainvert), .Less(1'b0), .Binvert(Binvert), .CarryIn(alu1bit_31_carryout), .Operation(OP),
    .A(A[31]), .B(B[31]), .CarryOut(C), .Set(alu1bit_32_set), .Result(N));
  not not_1 (not_1_out, A[31]);
  not not_2 (not_2_out, B[31]);
  not not_3 (not_3_out, alu1bit_31_carryout);
  and and_1 (and_1_out, alu1bit_31_carryout, not_1_out, not_2_out);
  and and_2 (and_2_out, not_3_out, A[31], B[31]);
  or or_1 (V, and_1_out, and_2_out);
  or or_2 (or_2_out, Result[0], Result[1], Result[2], Result[3], Result[4], Result[5], Result[6], Result[7], Result[8], Result[9], Result[10], Result[11], Result[12], Result[13], Result[14], Result[15], Result[16], Result[17], Result[18], Result[19], Result[20], Result[21], Result[22], Result[23], Result[24], Result[25], Result[26], Result[27], Result[28], Result[29], Result[30], N, 1'b0);
  not not_4 (Z, or_2_out);

  assign Result[31] = N;
endmodule

module temp (
  input  [3:0] ALUOp,
  input  A,
  input  B,
  input  Less,
  output Result,
  output C,
  output Set
);

  ALU1Bit alu1bit_1 (
    .Ainvert(ALUOp[3]), .Less(Less), .Binvert(ALUOp[2]), .CarryIn(ALUOp[2]), .Operation(ALUOp[1:0]), .A(A),
    .B(B), .CarryOut(C), .Set(Set), .Result(Result));
endmodule

module temp_top (
  input  [3:0] in_1,
  input  in_2,
  input  in_3,
  input  in_4,
  output out_5
);

  temp temp_1 (.ALUOp(in_1), .A(in_2), .B(in_3), .Less(in_4), .Result(out_5));  // open: C, Set
endmodule

module ALU32BitTester (
  input  [31:0] in_1,
  input  in_2,
  input  in_3,
  input  [1:0] in_4,
  input  [31:0] in_5,
  output [31:0] out_6,
  output out_7,
  output out_8,
  output out_9,
  output out_10
);

  ALU32Bit alu32bit_1 (
    .Ainvert(in_3), .Binvert(in_2), .OP(in_4), .B(in_5), .A(in_1), .Result(out_6), .N(out_8), .C(out_9),
    .V(out_10), .Z(out_7));
endmodule

module PCPath (
  input  [31:0] D,
  input  in_2,
  output [31:0] SUM,
  output [31:0] ReadAddress
);

  Register32BitDFlipFlops register32bitdflipflops_1 (.Clock(in_2), .D(D), .Q(ReadAddress));
  Adder #(.width(32)) adder_1 (.a(ReadAddress), .b(32'h4), .out(SUM), .cin(1'b0));  // open: cout
endmodule

module Clocked_D_FlipFlop (
  input  D,
  input  Clock,
  output Q,
  output Q_Bar
);

  wire nand_1_out, nand_2_out, nand_3_out, nand_4_out, nand_5_out, nand_6_out, not_1_out, not_2_out;

  nand nand_1 (nand_1_out, D, Clock);
  nand nand_2 (nand_2_out, Clock, not_1_out);
  not not_1 (not_1_out, D);
  nand nand_3 (nand_3_out, nand_1_out, nand_4_out);
  nand nand_4 (nand_4_out, nand_3_out, nand_2_out);
  not not_2 (not_2_out, Clock);
  nand nand_5 (nand_5_out, nand_3_out, not_2_out);
  nand nand_6 (nand_6_out, not_2_out, nand_4_out);
  nand nand_7 (Q, nand_5_out, Q_Bar);
  nand nand_8 (Q_Bar, Q, nand_6_out);
endmodule

module Register32Bits (
  input  Clock,
  input  [31:0] D,
  output [31:0] Q
);

  Clocked_D_FlipFlop clocked_d_flipflop_1 (.D(D[0]), .Clock(Clock), .Q(Q[0]));  // open: Q_Bar
  Clocked_D_FlipFlop clocked_d_flipflop_2 (.D(D[1]), .Clock(Clock), .Q(Q[1]));  // open: Q_Bar
  Clocked_D_FlipFlop clocked_d_flipflop_3 (.D(D[2]), .Clock(Clock), .Q(Q[2]));  // open: Q_Bar
  Clocked_D_FlipFlop clocked_d_flipflop_4 (.D(D[3]), .Clock(Clock), .Q(Q[3]));  // open: Q_Bar
  Clocked_D_FlipFlop clocked_d_flipflop_5 (.D(D[4]), .Clock(Clock), .Q(Q[4]));  // open: Q_Bar
  Clocked_D_FlipFlop clocked_d_flipflop_6 (.D(D[5]), .Clock(Clock), .Q(Q[5]));  // open: Q_Bar
  Clocked_D_FlipFlop clocked_d_flipflop_7 (.D(D[6]), .Clock(Clock), .Q(Q[6]));  // open: Q_Bar
  Clocked_D_FlipFlop clocked_d_flipflop_8 (.D(D[7]), .Clock(Clock), .Q(Q[7]));  // open: Q_Bar
  Clocked_D_FlipFlop clocked_d_flipflop_9 (.D(D[8]), .Clock(Clock), .Q(Q[8]));  // open: Q_Bar
  Clocked_D_FlipFlop clocked_d_flipflop_10 (.D(D[9]), .Clock(Clock), .Q(Q[9]));  // open: Q_Bar
  Clocked_D_FlipFlop clocked_d_flipflop_11 (.D(D[10]), .Clock(Clock), .Q(Q[10]));  // open: Q_Bar
  Clocked_D_FlipFlop clocked_d_flipflop_12 (.D(D[11]), .Clock(Clock), .Q(Q[11]));  // open: Q_Bar
  Clocked_D_FlipFlop clocked_d_flipflop_13 (.D(D[12]), .Clock(Clock), .Q(Q[12]));  // open: Q_Bar
  Clocked_D_FlipFlop clocked_d_flipflop_14 (.D(D[13]), .Clock(Clock), .Q(Q[13]));  // open: Q_Bar
  Clocked_D_FlipFlop clocked_d_flipflop_15 (.D(D[14]), .Clock(Clock), .Q(Q[14]));  // open: Q_Bar
  Clocked_D_FlipFlop clocked_d_flipflop_16 (.D(D[15]), .Clock(Clock), .Q(Q[15]));  // open: Q_Bar
  Clocked_D_FlipFlop clocked_d_flipflop_17 (.D(D[16]), .Clock(Clock), .Q(Q[16]));  // open: Q_Bar
  Clocked_D_FlipFlop clocked_d_flipflop_18 (.D(D[17]), .Clock(Clock), .Q(Q[17]));  // open: Q_Bar
  Clocked_D_FlipFlop clocked_d_flipflop_19 (.D(D[18]), .Clock(Clock), .Q(Q[18]));  // open: Q_Bar
  Clocked_D_FlipFlop clocked_d_flipflop_20 (.D(D[19]), .Clock(Clock), .Q(Q[19]));  // open: Q_Bar
  Clocked_D_FlipFlop clocked_d_flipflop_21 (.D(D[20]), .Clock(Clock), .Q(Q[20]));  // open: Q_Bar
  Clocked_D_FlipFlop clocked_d_flipflop_22 (.D(D[21]), .Clock(Clock), .Q(Q[21]));  // open: Q_Bar
  Clocked_D_FlipFlop clocked_d_flipflop_23 (.D(D[22]), .Clock(Clock), .Q(Q[22]));  // open: Q_Bar
  Clocked_D_FlipFlop clocked_d_flipflop_24 (.D(D[23]), .Clock(Clock), .Q(Q[23]));  // open: Q_Bar
  Clocked_D_FlipFlop clocked_d_flipflop_25 (.D(D[24]), .Clock(Clock), .Q(Q[24]));  // open: Q_Bar
  Clocked_D_FlipFlop clocked_d_flipflop_26 (.D(D[25]), .Clock(Clock), .Q(Q[25]));  // open: Q_Bar
  Clocked_D_FlipFlop clocked_d_flipflop_27 (.D(D[26]), .Clock(Clock), .Q(Q[26]));  // open: Q_Bar
  Clocked_D_FlipFlop clocked_d_flipflop_28 (.D(D[27]), .Clock(Clock), .Q(Q[27]));  // open: Q_Bar
  Clocked_D_FlipFlop clocked_d_flipflop_29 (.D(D[28]), .Clock(Clock), .Q(Q[28]));  // open: Q_Bar
  Clocked_D_FlipFlop clocked_d_flipflop_30 (.D(D[29]), .Clock(Clock), .Q(Q[29]));  // open: Q_Bar
  Clocked_D_FlipFlop clocked_d_flipflop_31 (.D(D[30]), .Clock(Clock), .Q(Q[30]));  // open: Q_Bar
  Clocked_D_FlipFlop clocked_d_flipflop_32 (.D(D[31]), .Clock(Clock), .Q(Q[31]));  // open: Q_Bar
endmodule

module Register32BitDFlipFlops (
  input  Clock,
  input  [31:0] D,
  output [31:0] Q
);

  D_Flip_Flop d_ff_1 (.D(D[0]), .clk(Clock), .Q(Q[0]));  // open: Qn, preset, reset
  D_Flip_Flop d_ff_2 (.D(D[1]), .clk(Clock), .Q(Q[1]));  // open: Qn, preset, reset
  D_Flip_Flop d_ff_3 (.D(D[2]), .clk(Clock), .Q(Q[2]));  // open: Qn, preset, reset
  D_Flip_Flop d_ff_4 (.D(D[3]), .clk(Clock), .Q(Q[3]));  // open: Qn, preset, reset
  D_Flip_Flop d_ff_5 (.D(D[4]), .clk(Clock), .Q(Q[4]));  // open: Qn, preset, reset
  D_Flip_Flop d_ff_6 (.D(D[5]), .clk(Clock), .Q(Q[5]));  // open: Qn, preset, reset
  D_Flip_Flop d_ff_7 (.D(D[6]), .clk(Clock), .Q(Q[6]));  // open: Qn, preset, reset
  D_Flip_Flop d_ff_8 (.D(D[7]), .clk(Clock), .Q(Q[7]));  // open: Qn, preset, reset
  D_Flip_Flop d_ff_9 (.D(D[8]), .clk(Clock), .Q(Q[8]));  // open: Qn, preset, reset
  D_Flip_Flop d_ff_10 (.D(D[9]), .clk(Clock), .Q(Q[9]));  // open: Qn, preset, reset
  D_Flip_Flop d_ff_11 (.D(D[10]), .clk(Clock), .Q(Q[10]));  // open: Qn, preset, reset
  D_Flip_Flop d_ff_12 (.D(D[11]), .clk(Clock), .Q(Q[11]));  // open: Qn, preset, reset
  D_Flip_Flop d_ff_13 (.D(D[12]), .clk(Clock), .Q(Q[12]));  // open: Qn, preset, reset
  D_Flip_Flop d_ff_14 (.D(D[13]), .clk(Clock), .Q(Q[13]));  // open: Qn, preset, reset
  D_Flip_Flop d_ff_15 (.D(D[14]), .clk(Clock), .Q(Q[14]));  // open: Qn, preset, reset
  D_Flip_Flop d_ff_16 (.D(D[15]), .clk(Clock), .Q(Q[15]));  // open: Qn, preset, reset
  D_Flip_Flop d_ff_17 (.D(D[16]), .clk(Clock), .Q(Q[16]));  // open: Qn, preset, reset
  D_Flip_Flop d_ff_18 (.D(D[17]), .clk(Clock), .Q(Q[17]));  // open: Qn, preset, reset
  D_Flip_Flop d_ff_19 (.D(D[18]), .clk(Clock), .Q(Q[18]));  // open: Qn, preset, reset
  D_Flip_Flop d_ff_20 (.D(D[19]), .clk(Clock), .Q(Q[19]));  // open: Qn, preset, reset
  D_Flip_Flop d_ff_21 (.D(D[20]), .clk(Clock), .Q(Q[20]));  // open: Qn, preset, reset
  D_Flip_Flop d_ff_22 (.D(D[21]), .clk(Clock), .Q(Q[21]));  // open: Qn, preset, reset
  D_Flip_Flop d_ff_23 (.D(D[22]), .clk(Clock), .Q(Q[22]));  // open: Qn, preset, reset
  D_Flip_Flop d_ff_24 (.D(D[23]), .clk(Clock), .Q(Q[23]));  // open: Qn, preset, reset
  D_Flip_Flop d_ff_25 (.D(D[24]), .clk(Clock), .Q(Q[24]));  // open: Qn, preset, reset
  D_Flip_Flop d_ff_26 (.D(D[25]), .clk(Clock), .Q(Q[25]));  // open: Qn, preset, reset
  D_Flip_Flop d_ff_27 (.D(D[26]), .clk(Clock), .Q(Q[26]));  // open: Qn, preset, reset
  D_Flip_Flop d_ff_28 (.D(D[27]), .clk(Clock), .Q(Q[27]));  // open: Qn, preset, reset
  D_Flip_Flop d_ff_29 (.D(D[28]), .clk(Clock), .Q(Q[28]));  // open: Qn, preset, reset
  D_Flip_Flop d_ff_30 (.D(D[29]), .clk(Clock), .Q(Q[29]));  // open: Qn, preset, reset
  D_Flip_Flop d_ff_31 (.D(D[30]), .clk(Clock), .Q(Q[30]));  // open: Qn, preset, reset
  D_Flip_Flop d_ff_32 (.D(D[31]), .clk(Clock), .Q(Q[31]));  // open: Qn, preset, reset
endmodule

module ControlUnit (
  input  [5:0] in_1,
  output RegDest,
  output ALUSrc,
  output MemtoReg,
  output RegWrite,
  output MemRead,
  output MemWrite,
  output Branch,
  output ALUOp1,
  output ALUOp2,
  output Jump
);

  and and_1 (ALUOp1, ~in_1[5], ~in_1[4], ~in_1[3], ~in_1[2], ~in_1[1], ~in_1[0]);  // AND_Gate
  and and_2 (MemRead, in_1[5], ~in_1[4], ~in_1[3], ~in_1[2], in_1[1], in_1[0]);  // AND_Gate
  and and_3 (MemWrite, in_1[5], ~in_1[4], in_1[3], ~in_1[2], in_1[1], in_1[0]);  // AND_Gate
  and and_4 (ALUOp2, ~in_1[5], ~in_1[4], ~in_1[3], in_1[2], ~in_1[1], ~in_1[0]);  // AND_Gate
  and and_5 (Jump, ~in_1[5], ~in_1[4], ~in_1[3], ~in_1[2], in_1[1], ~in_1[0]);  // AND_Gate
  or or_1 (ALUSrc, MemRead, MemWrite);
  or or_2 (RegWrite, ALUOp1, MemRead);

  assign Branch = ALUOp2;
  assign MemtoReg = MemRead;
  assign RegDest = ALUOp1;
endmodule

module ALUControl (
  input  ALUOp1,
  input  ALUOp0,
  input  Funct0,
  input  Funct1,
  input  Funct2,
  input  Funct3,
  input  Funct4,
  input  Funct5,
  output ALUCont0,
  output ALUCont1,
  output ALUCont2,
  output ALUCont3
);

  wire and_1_out, and_2_out, and_3_out, and_4_out, and_5_out, and_6_out, and_7_out, and_8_out, not_1_out;

  and and_1 (and_1_out, ALUOp1, ~ALUOp0, Funct0, ~Funct1, Funct2, ~Funct3, Funct4, ~Funct5);  // AND_Gate
  and and_2 (and_2_out, ALUOp1, ~ALUOp0, Funct0, ~Funct1, ~Funct2, Funct3, ~Funct4, Funct5);  // AND_Gate
  and and_3 (and_3_out, ~ALUOp1, ~ALUOp0, Funct0, Funct1, Funct2, Funct3, Funct4, Funct5);  // AND_Gate
  and and_4 (and_4_out, ~ALUOp1, ~ALUOp0, Funct0, Funct1, Funct2, Funct3, Funct4, Funct5);  // AND_Gate
  and and_5 (and_5_out, ~ALUOp1, ALUOp0, Funct0, Funct1, Funct2, Funct3, Funct4, Funct5);  // AND_Gate
  and and_6 (and_6_out, ALUOp1, ~ALUOp0, Funct0, ~Funct1, ~Funct2, ~Funct3, ~Funct4, ~Funct5);  // AND_Gate
  and and_7 (and_7_out, ALUOp1, ~ALUOp0, Funct0, ~Funct1, ~Funct2, ~Funct3, Funct4, ~Funct5);  // AND_Gate
  and and_8 (and_8_out, ALUOp1, ~ALUOp0, Funct0, ~Funct1, ~Funct2, Funct3, ~Funct4, ~Funct5);  // AND_Gate
  not not_1 (not_1_out, ALUOp1);
  or or_1 (ALUCont0, and_1_out, and_2_out);
  or or_2 (ALUCont1, and_3_out, and_4_out, and_5_out, not_1_out, and_6_out, and_7_out, and_1_out);
  or or_3 (ALUCont2, and_5_out, ALUOp0, and_7_out, and_1_out);

  assign ALUCont3 = 1'b0;
endmodule

module RegisterGroup (
  input  RegWrite,
  input  CLK,
  input  [4:0] ReadReg1,
  input  [4:0] WriteReg,
  input  [4:0] ReadReg2,
  input  [31:0] WriteData,
  output [31:0] ReadData1,
  output [31:0] ReadData2
);

  wire and_1_out, and_2_out, and_3_out, and_4_out, and_5_out, and_6_out, and_7_out, and_8_out, and_9_out,
       and_10_out, and_11_out, and_12_out, and_13_out, and_14_out, and_15_out, and_16_out, and_17_out,
       and_18_out, and_19_out, and_20_out, and_21_out, and_22_out, and_23_out, and_24_out, and_25_out,
       and_26_out, and_27_out, and_28_out, and_29_out, and_30_out, and_31_out, and_32_out, decoder_1_out0,
       decoder_1_out1, decoder_1_out2, decoder_1_out3, decoder_1_out4, decoder_1_out5, decoder_1_out6,
       decoder_1_out7, decoder_1_out8, decoder_1_out9, decoder_1_out10, decoder_1_out11, decoder_1_out12,
       decoder_1_out13, decoder_1_out14, decoder_1_out15, decoder_1_out16, decoder_1_out17, decoder_1_out18,
       decoder_1_out19, decoder_1_out20, decoder_1_out21, decoder_1_out22, decoder_1_out23, decoder_1_out24,
       decoder_1_out25, decoder_1_out26, decoder_1_out27, decoder_1_out28, decoder_1_out29, decoder_1_out30,
       decoder_1_out31;
  wire [31:0] register32bits_1_q, register32bits_2_q, register32bits_3_q, register32bits_4_q,
       register32bits_5_q, register32bits_6_q, register32bits_7_q, register32bits_8_q, register32bits_9_q,
       register32bits_10_q, register32bits_11_q, register32bits_12_q, register32bits_13_q,
       register32bits_14_q, register32bits_15_q, register32bits_16_q, register32bits_17_q,
       register32bits_18_q, register32bits_19_q, register32bits_20_q, register32bits_21_q,
       register32bits_22_q, register32bits_23_q, register32bits_24_q, register32bits_25_q,
       register32bits_26_q, register32bits_27_q, register32bits_28_q, register32bits_29_q,
       register32bits_30_q, register32bits_31_q, register32bits_32_q;

  Decoder #(.enable("false"), .select(5)) decoder_1 (
    .out0(decoder_1_out0), .out1(decoder_1_out1), .out2(decoder_1_out2), .out3(decoder_1_out3),
    .out4(decoder_1_out4), .out5(decoder_1_out5), .out6(decoder_1_out6), .out7(decoder_1_out7),
    .out8(decoder_1_out8), .out9(decoder_1_out9), .out10(decoder_1_out10), .out11(decoder_1_out11),
    .out12(decoder_1_out12), .out13(decoder_1_out13), .out14(decoder_1_out14), .out15(decoder_1_out15),
    .out16(decoder_1_out16), .out17(decoder_1_out17), .out18(decoder_1_out18), .out19(decoder_1_out19),
    .out20(decoder_1_out20), .out21(decoder_1_out21), .out22(decoder_1_out22), .out23(decoder_1_out23),
    .out24(decoder_1_out24), .out25(decoder_1_out25), .out26(decoder_1_out26), .out27(decoder_1_out27),
    .out28(decoder_1_out28), .out29(decoder_1_out29), .out30(decoder_1_out30), .out31(decoder_1_out31),
    .sel(WriteReg));
  and and_1 (and_1_out, CLK, RegWrite, decoder_1_out0);
  and and_2 (and_2_out, CLK, RegWrite, decoder_1_out1);
  and and_3 (and_3_out, CLK, RegWrite, decoder_1_out2);
  and and_4 (and_4_out, CLK, RegWrite, decoder_1_out3);
  and and_5 (and_5_out, CLK, RegWrite, decoder_1_out4);
  and and_6 (and_6_out, CLK, RegWrite, decoder_1_out5);
  and and_7 (and_7_out, CLK, RegWrite, decoder_1_out6);
  and and_8 (and_8_out, CLK, RegWrite, decoder_1_out7);
  and and_9 (and_9_out, CLK, RegWrite, decoder_1_out8);
  and and_10 (and_10_out, CLK, RegWrite, decoder_1_out9);
  and and_11 (and_11_out, CLK, RegWrite, decoder_1_out10);
  and and_12 (and_12_out, CLK, RegWrite, decoder_1_out11);
  and and_13 (and_13_out, CLK, RegWrite, decoder_1_out12);
  and and_14 (and_14_out, CLK, RegWrite, decoder_1_out13);
  and and_15 (and_15_out, CLK, RegWrite, decoder_1_out14);
  and and_16 (and_16_out, CLK, RegWrite, decoder_1_out15);
  and and_17 (and_17_out, CLK, RegWrite, decoder_1_out16);
  and and_18 (and_18_out, CLK, RegWrite, decoder_1_out17);
  and and_19 (and_19_out, CLK, RegWrite, decoder_1_out18);
  and and_20 (and_20_out, CLK, RegWrite, decoder_1_out19);
  and and_21 (and_21_out, CLK, RegWrite, decoder_1_out20);
  and and_22 (and_22_out, CLK, RegWrite, decoder_1_out21);
  and and_23 (and_23_out, CLK, RegWrite, decoder_1_out22);
  and and_24 (and_24_out, CLK, RegWrite, decoder_1_out23);
  and and_25 (and_25_out, CLK, RegWrite, decoder_1_out24);
  and and_26 (and_26_out, CLK, RegWrite, decoder_1_out25);
  and and_27 (and_27_out, CLK, RegWrite, decoder_1_out26);
  and and_28 (and_28_out, CLK, RegWrite, decoder_1_out27);
  and and_29 (and_29_out, CLK, RegWrite, decoder_1_out28);
  and and_30 (and_30_out, CLK, RegWrite, decoder_1_out29);
  and and_31 (and_31_out, CLK, RegWrite, decoder_1_out30);
  and and_32 (and_32_out, CLK, RegWrite, decoder_1_out31);
  Register32Bits register32bits_1 (.Clock(and_1_out), .D(WriteData), .Q(register32bits_1_q));
  Register32Bits register32bits_2 (.Clock(and_2_out), .D(WriteData), .Q(register32bits_2_q));
  Register32Bits register32bits_3 (.Clock(and_3_out), .D(WriteData), .Q(register32bits_3_q));
  Register32Bits register32bits_4 (.Clock(and_4_out), .D(WriteData), .Q(register32bits_4_q));
  Register32Bits register32bits_5 (.Clock(and_5_out), .D(WriteData), .Q(register32bits_5_q));
  Register32Bits register32bits_6 (.Clock(and_6_out), .D(WriteData), .Q(register32bits_6_q));
  Register32Bits register32bits_7 (.Clock(and_7_out), .D(WriteData), .Q(register32bits_7_q));
  Register32Bits register32bits_8 (.Clock(and_8_out), .D(WriteData), .Q(register32bits_8_q));
  Register32Bits register32bits_9 (.Clock(and_9_out), .D(WriteData), .Q(register32bits_9_q));
  Register32Bits register32bits_10 (.Clock(and_10_out), .D(WriteData), .Q(register32bits_10_q));
  Register32Bits register32bits_11 (.Clock(and_11_out), .D(WriteData), .Q(register32bits_11_q));
  Register32Bits register32bits_12 (.Clock(and_12_out), .D(WriteData), .Q(register32bits_12_q));
  Register32Bits register32bits_13 (.Clock(and_13_out), .D(WriteData), .Q(register32bits_13_q));
  Register32Bits register32bits_14 (.Clock(and_14_out), .D(WriteData), .Q(register32bits_14_q));
  Register32Bits register32bits_15 (.Clock(and_15_out), .D(WriteData), .Q(register32bits_15_q));
  Register32Bits register32bits_16 (.Clock(and_16_out), .D(WriteData), .Q(register32bits_16_q));
  Register32Bits register32bits_17 (.Clock(and_17_out), .D(WriteData), .Q(register32bits_17_q));
  Register32Bits register32bits_18 (.Clock(and_18_out), .Q(register32bits_18_q));  // open: D
  Register32Bits register32bits_19 (.Clock(and_19_out), .D(WriteData), .Q(register32bits_19_q));
  Register32Bits register32bits_20 (.Clock(and_20_out), .D(WriteData), .Q(register32bits_20_q));
  Register32Bits register32bits_21 (.Clock(and_21_out), .D(WriteData), .Q(register32bits_21_q));
  Register32Bits register32bits_22 (.Clock(and_22_out), .D(WriteData), .Q(register32bits_22_q));
  Register32Bits register32bits_23 (.Clock(and_23_out), .D(WriteData), .Q(register32bits_23_q));
  Register32Bits register32bits_24 (.Clock(and_24_out), .D(WriteData), .Q(register32bits_24_q));
  Register32Bits register32bits_25 (.Clock(and_25_out), .D(WriteData), .Q(register32bits_25_q));
  Register32Bits register32bits_26 (.Clock(and_26_out), .D(WriteData), .Q(register32bits_26_q));
  Register32Bits register32bits_27 (.Clock(and_27_out), .D(WriteData), .Q(register32bits_27_q));
  Register32Bits register32bits_28 (.Clock(and_28_out), .D(WriteData), .Q(register32bits_28_q));
  Register32Bits register32bits_29 (.Clock(and_29_out), .D(WriteData), .Q(register32bits_29_q));
  Register32Bits register32bits_30 (.Clock(and_30_out), .D(WriteData), .Q(register32bits_30_q));
  Register32Bits register32bits_31 (.Clock(and_31_out), .D(WriteData), .Q(register32bits_31_q));
  Register32Bits register32bits_32 (.Clock(and_32_out), .D(WriteData), .Q(register32bits_32_q));
  Multiplexer #(.select(5), .width(32)) multiplexer_1 (
    .in0(register32bits_1_q), .in1(register32bits_2_q), .in2(register32bits_3_q), .in3(register32bits_4_q),
    .in4(register32bits_5_q), .in5(register32bits_6_q), .in6(register32bits_7_q), .in7(register32bits_8_q),
    .in8(register32bits_9_q), .in9(register32bits_10_q), .in10(register32bits_11_q),
    .in11(register32bits_12_q), .in12(register32bits_13_q), .in13(register32bits_14_q),
    .in14(register32bits_15_q), .in15(register32bits_16_q), .in16(register32bits_17_q),
    .in17(register32bits_18_q), .in18(register32bits_19_q), .in19(register32bits_20_q),
    .in20(register32bits_21_q), .in21(register32bits_22_q), .in22(register32bits_23_q),
    .in23(register32bits_24_q), .in24(register32bits_25_q), .in25(register32bits_26_q),
    .in26(register32bits_27_q), .in27(register32bits_28_q), .in28(register32bits_29_q),
    .in29(register32bits_30_q), .in30(register32bits_31_q), .in31(register32bits_32_q), .out(ReadData1),
    .sel(ReadReg1));
  Multiplexer #(.select(5), .width(32)) multiplexer_2 (
    .in0(register32bits_1_q), .in1(register32bits_2_q), .in2(register32bits_3_q), .in3(register32bits_4_q),
    .in4(register32bits_5_q), .in5(register32bits_6_q), .in6(register32bits_7_q), .in7(register32bits_8_q),
    .in8(register32bits_9_q), .in9(register32bits_10_q), .in10(register32bits_11_q),
    .in11(register32bits_12_q), .in12(register32bits_13_q), .in13(register32bits_14_q),
    .in14(register32bits_15_q), .in15(register32bits_16_q), .in16(register32bits_17_q),
    .in17(register32bits_18_q), .in18(register32bits_19_q), .in19(register32bits_20_q),
    .in20(register32bits_21_q), .in21(register32bits_22_q), .in22(register32bits_23_q),
    .in23(register32bits_24_q), .in24(register32bits_25_q), .in25(register32bits_26_q),
    .in26(register32bits_27_q), .in27(register32bits_28_q), .in28(register32bits_29_q),
    .in29(register32bits_30_q), .in30(register32bits_31_q), .in31(register32bits_32_q), .out(ReadData2),
    .sel(ReadReg2));
endmodule

module RegisterTest (
  input  in_1,
  input  in_2,
  input  [4:0] in_3,
  input  [4:0] in_4,
  input  [4:0] in_5,
  input  [31:0] in_6,
  output [31:0] out_7,
  output [31:0] out_8
);

  RegisterGroup registergroup_1 (
    .RegWrite(in_1), .CLK(in_2), .ReadReg1(in_3), .WriteReg(in_4), .ReadReg2(in_5), .WriteData(in_6),
    .ReadData1(out_7), .ReadData2(out_8));
endmodule
