// Logisim project CounterPathAndControlUnit.circ as structural Verilog: 6 circuits, main circuit Clocked_D_FlipFlop
module PCPath (
  input  in_1,
  output [31:0] ReadAddress
);

  wire [31:0] adder_1_out;

  Register32BitDFlipFlops register32bitdflipflops_1 (.Clock(in_1), .D(adder_1_out), .Q(ReadAddress));
  Adder #(.width(32)) adder_1 (.a(ReadAddress), .b(32'h4), .out(adder_1_out), .cin(1'b0));  // open: cout
endmodule

module Clocked_D_FlipFlop (
  input  D,
  input  Clock,
  output Q,
  output Q_Bar
);

  wire nand_1_out, nand_2_out, nand_3_out, nand_4_out, nand_5_out, nand_6_out, not_1_out, not_2_out;

  nand nand_1 (nand_1_out, D, Clock);
  nand nand_2 (nand_2_out, Clock, not_1_out);
  not not_1 (not_1_out, D);
  nand nand_3 (nand_3_out, nand_1_out, nand_4_out);
  nand nand_4 (nand_4_out, nand_3_out, nand_2_out);
  not not_2 (not_2_out, Clock);
  nand nand_5 (nand_5_out, nand_3_out, not_2_out);
  nand nand_6 (nand_6_out, not_2_out, nand_4_out);
  nand nand_7 (Q, nand_5_out, Q_Bar);
  nand nand_8 (Q_Bar, Q, nand_6_out);
endmodule

module Register32Bits (
  input  Clock,
  input  [31:0] D,
  output [31:0] Q
);

  Clocked_D_FlipFlop clocked_d_flipflop_1 (.D(D[0]), .Clock(Clock), .Q(Q[0]));  // open: Q_Bar
  Clocked_D_FlipFlop clocked_d_flipflop_2 (.D(D[1]), .Clock(Clock), .Q(Q[1]));  // open: Q_Bar
  Clocked_D_FlipFlop clocked_d_flipflop_3 (.D(D[2]), .Clock(Clock), .Q(Q[2]));  // open: Q_Bar
  Clocked_D_FlipFlop clocked_d_flipflop_4 (.D(D[3]), .Clock(Clock), .Q(Q[3]));  // open: Q_Bar
  Clocked_D_FlipFlop clocked_d_flipflop_5 (.D(D[4]), .Clock(Clock), .Q(Q[4]));  // open: Q_Bar
  Clocked_D_FlipFlop clocked_d_flipflop_6 (.D(D[5]), .Clock(Clock), .Q(Q[5]));  // open: Q_Bar
  Clocked_D_FlipFlop clocked_d_flipflop_7 (.D(D[6]), .Clock(Clock), .Q(Q[6]));  // open: Q_Bar
  Clocked_D_FlipFlop clocked_d_flipflop_8 (.D(D[7]), .Clock(Clock), .Q(Q[7]));  // open: Q_Bar
  Clocked_D_FlipFlop clocked_d_flipflop_9 (.D(D[8]), .Clock(Clock), .Q(Q[8]));  // open: Q_Bar
  Clocked_D_FlipFlop clocked_d_flipflop_10 (.D(D[9]), .Clock(Clock), .Q(Q[9]));  // open: Q_Bar
  Clocked_D_FlipFlop clocked_d_flipflop_11 (.D(D[10]), .Clock(Clock), .Q(Q[10]));  // open: Q_Bar
  Clocked_D_FlipFlop clocked_d_flipflop_12 (.D(D[11]), .Clock(Clock), .Q(Q[11]));  // open: Q_Bar
  Clocked_D_FlipFlop clocked_d_flipflop_13 (.D(D[12]), .Clock(Clock), .Q(Q[12]));  // open: Q_Bar
  Clocked_D_FlipFlop clocked_d_flipflop_14 (.D(D[13]), .Clock(Clock), .Q(Q[13]));  // open: Q_Bar
  Clocked_D_FlipFlop clocked_d_flipflop_15 (.D(D[14]), .Clock(Clock), .Q(Q[14]));  // open: Q_Bar
  Clocked_D_FlipFlop clocked_d_flipflop_16 (.D(D[15]), .Clock(Clock), .Q(Q[15]));  // open: Q_Bar
  Clocked_D_FlipFlop clocked_d_flipflop_17 (.D(D[16]), .Clock(Clock), .Q(Q[16]));  // open: Q_Bar
  Clocked_D_FlipFlop clocked_d_flipflop_18 (.D(D[17]), .Clock(Clock), .Q(Q[17]));  // open: Q_Bar
  Clocked_D_FlipFlop clocked_d_flipflop_19 (.D(D[18]), .Clock(Clock), .Q(Q[18]));  // open: Q_Bar
  Clocked_D_FlipFlop clocked_d_flipflop_20 (.D(D[19]), .Clock(Clock), .Q(Q[19]));  // open: Q_Bar
  Clocked_D_FlipFlop clocked_d_flipflop_21 (.D(D[20]), .Clock(Clock), .Q(Q[20]));  // open: Q_Bar
  Clocked_D_FlipFlop clocked_d_flipflop_22 (.D(D[21]), .Clock(Clock), .Q(Q[21]));  // open: Q_Bar
  Clocked_D_FlipFlop clocked_d_flipflop_23 (.D(D[22]), .Clock(Clock), .Q(Q[22]));  // open: Q_Bar
  Clocked_D_FlipFlop clocked_d_flipflop_24 (.D(D[23]), .Clock(Clock), .Q(Q[23]));  // open: Q_Bar
  Clocked_D_FlipFlop clocked_d_flipflop_25 (.D(D[24]), .Clock(Clock), .Q(Q[24]));  // open: Q_Bar
  Clocked_D_FlipFlop clocked_d_flipflop_26 (.D(D[25]), .Clock(Clock), .Q(Q[25]));  // open: Q_Bar
  Clocked_D_FlipFlop clocked_d_flipflop_27 (.D(D[26]), .Clock(Clock), .Q(Q[26]));  // open: Q_Bar
  Clocked_D_FlipFlop clocked_d_flipflop_28 (.D(D[27]), .Clock(Clock), .Q(Q[27]));  // open: Q_Bar
  Clocked_D_FlipFlop clocked_d_flipflop_29 (.D(D[28]), .Clock(Clock), .Q(Q[28]));  // open: Q_Bar
  Clocked_D_FlipFlop clocked_d_flipflop_30 (.D(D[29]), .Clock(Clock), .Q(Q[29]));  // open: Q_Bar
  Clocked_D_FlipFlop clocked_d_flipflop_31 (.D(D[30]), .Clock(Clock), .Q(Q[30]));  // open: Q_Bar
  Clocked_D_FlipFlop clocked_d_flipflop_32 (.D(D[31]), .Clock(Clock), .Q(Q[31]));  // open: Q_Bar
endmodule

module Register32BitDFlipFlops (
  input  Clock,
  input  [31:0] D,
  output [31:0] Q
);

  D_Flip_Flop d_ff_1 (.D(D[0]), .clk(Clock), .Q(Q[0]));  // open: Qn, preset, reset
  D_Flip_Flop d_ff_2 (.D(D[1]), .clk(Clock), .Q(Q[1]));  // open: Qn, preset, reset
  D_Flip_Flop d_ff_3 (.D(D[2]), .clk(Clock), .Q(Q[2]));  // open: Qn, preset, reset
  D_Flip_Flop d_ff_4 (.D(D[3]), .clk(Clock), .Q(Q[3]));  // open: Qn, preset, reset
  D_Flip_Flop d_ff_5 (.D(D[4]), .clk(Clock), .Q(Q[4]));  // open: Qn, preset, reset
  D_Flip_Flop d_ff_6 (.D(D[5]), .clk(Clock), .Q(Q[5]));  // open: Qn, preset, reset
  D_Flip_Flop d_ff_7 (.D(D[6]), .clk(Clock), .Q(Q[6]));  // open: Qn, preset, reset
  D_Flip_Flop d_ff_8 (.D(D[7]), .clk(Clock), .Q(Q[7]));  // open: Qn, preset, reset
  D_Flip_Flop d_ff_9 (.D(D[8]), .clk(Clock), .Q(Q[8]));  // open: Qn, preset, reset
  D_Flip_Flop d_ff_10 (.D(D[9]), .clk(Clock), .Q(Q[9]));  // open: Qn, preset, reset
  D_Flip_Flop d_ff_11 (.D(D[10]), .clk(Clock), .Q(Q[10]));  // open: Qn, preset, reset
  D_Flip_Flop d_ff_12 (.D(D[11]), .clk(Clock), .Q(Q[11]));  // open: Qn, preset, reset
  D_Flip_Flop d_ff_13 (.D(D[12]), .clk(Clock), .Q(Q[12]));  // open: Qn, preset, reset
  D_Flip_Flop d_ff_14 (.D(D[13]), .clk(Clock), .Q(Q[13]));  // open: Qn, preset, reset
  D_Flip_Flop d_ff_15 (.D(D[14]), .clk(Clock), .Q(Q[14]));  // open: Qn, preset, reset
  D_Flip_Flop d_ff_16 (.D(D[15]), .clk(Clock), .Q(Q[15]));  // open: Qn, preset, reset
  D_Flip_Flop d_ff_17 (.D(D[16]), .clk(Clock), .Q(Q[16]));  // open: Qn, preset, reset
  D_Flip_Flop d_ff_18 (.D(D[17]), .clk(Clock), .Q(Q[17]));  // open: Qn, preset, reset
  D_Flip_Flop d_ff_19 (.D(D[18]), .clk(Clock), .Q(Q[18]));  // open: Qn, preset, reset
  D_Flip_Flop d_ff_20 (.D(D[19]), .clk(Clock), .Q(Q[19]));  // open: Qn, preset, reset
  D_Flip_Flop d_ff_21 (.D(D[20]), .clk(Clock), .Q(Q[20]));  // open: Qn, preset, reset
  D_Flip_Flop d_ff_22 (.D(D[21]), .clk(Clock), .Q(Q[21]));  // open: Qn, preset, reset
  D_Flip_Flop d_ff_23 (.D(D[22]), .clk(Clock), .Q(Q[22]));  // open: Qn, preset, reset
  D_Flip_Flop d_ff_24 (.D(D[23]), .clk(Clock), .Q(Q[23]));  // open: Qn, preset, reset
  D_Flip_Flop d_ff_25 (.D(D[24]), .clk(Clock), .Q(Q[24]));  // open: Qn, preset, reset
  D_Flip_Flop d_ff_26 (.D(D[25]), .clk(Clock), .Q(Q[25]));  // open: Qn, preset, reset
  D_Flip_Flop d_ff_27 (.D(D[26]), .clk(Clock), .Q(Q[26]));  // open: Qn, preset, reset
  D_Flip_Flop d_ff_28 (.D(D[27]), .clk(Clock), .Q(Q[27]));  // open: Qn, preset, reset
  D_Flip_Flop d_ff_29 (.D(D[28]), .clk(Clock), .Q(Q[28]));  // open: Qn, preset, reset
  D_Flip_Flop d_ff_30 (.D(D[29]), .clk(Clock), .Q(Q[29]));  // open: Qn, preset, reset
  D_Flip_Flop d_ff_31 (.D(D[30]), .clk(Clock), .Q(Q[30]));  // open: Qn, preset, reset
  D_Flip_Flop d_ff_32 (.D(D[31]), .clk(Clock), .Q(Q[31]));  // open: Qn, preset, reset
endmodule

module ControlUnit (
  input  [5:0] in_1,
  output RegDest,
  output ALUSrc,
  output MemtoReg,
  output RegWrite,
  output MemRead,
  output MemWrite,
  output Branch,
  output ALUOp1,
  output ALUOp2,
  output Jump
);

  and and_1 (ALUOp1, ~in_1[5], ~in_1[4], ~in_1[3], ~in_1[2], ~in_1[1], ~in_1[0]);  // AND_Gate
  and and_2 (MemRead, in_1[5], ~in_1[4], ~in_1[3], ~in_1[2], in_1[1], in_1[0]);  // AND_Gate
  and and_3 (MemWrite, in_1[5], ~in_1[4], in_1[3], ~in_1[2], in_1[1], in_1[0]);  // AND_Gate
  and and_4 (ALUOp2, ~in_1[5], ~in_1[4], ~in_1[3], in_1[2], ~in_1[1], ~in_1[0]);  // AND_Gate
  and and_5 (Jump, ~in_1[5], ~in_1[4], ~in_1[3], ~in_1[2], in_1[1], ~in_1[0]);  // AND_Gate
  or or_1 (ALUSrc, MemRead, MemWrite);
  or or_2 (RegWrite, ALUOp1, ALUOp1);

  assign Branch = ALUOp2;
  assign MemtoReg = MemRead;
  assign RegDest = ALUOp1;
endmodule

module ALUControl (
  input  ALUOp1,
  input  ALUOp2,
  input  Funct0,
  input  Funct1,
  input  Funct2,
  input  Funct3,
  input  Funct4,
  input  Funct5,
  output ALUCont0,
  output ALUCont1,
  output ALUCont2,
  output ALUCont3
);

  wire and_1_out, and_2_out, and_3_out, and_4_out, and_5_out, and_6_out, and_7_out;

  and and_1 (and_1_out, ALUOp1, ~ALUOp2, Funct0, ~Funct1, Funct2, ~Funct3, Funct4, ~Funct5);  // AND_Gate
  and and_2 (and_2_out, ALUOp1, ~ALUOp2, Funct0, ~Funct1, ~Funct2, Funct3, ~Funct4, Funct5);  // AND_Gate
  and and_3 (and_3_out, ~ALUOp1, ~ALUOp2, Funct0, Funct1, Funct2, Funct3, Funct4, Funct5);  // AND_Gate
  and and_4 (and_4_out, ~ALUOp1, ~ALUOp2, Funct0, Funct1, Funct2, Funct3, Funct4, Funct5);  // AND_Gate
  and and_5 (and_5_out, ~ALUOp1, ALUOp2, Funct0, Funct1, Funct2, Funct3, Funct4, Funct5);  // AND_Gate
  and and_6 (and_6_out, ALUOp1, ~ALUOp2, Funct0, ~Funct1, ~Funct2, ~Funct3, ~Funct4, ~Funct5);  // AND_Gate
  and and_7 (and_7_out, ALUOp1, ~ALUOp2, Funct0, ~Funct1, ~Funct2, ~Funct3, Funct4, ~Funct5);  // AND_Gate
  // AND_Gate and_8 has open pins: in0=ALUOp1, in1=ALUOp2, in2=Funct0, in3=Funct1, in4=Funct2, in5=Funct3, in6=Funct4, in7=Funct5, out=open
  or or_1 (ALUCont0, and_1_out, and_2_out);
  or or_2 (ALUCont1, and_3_out, and_4_out, and_5_out, and_6_out, and_7_out, and_1_out);
  or or_3 (ALUCont2, and_1_out, and_3_out, and_6_out);

  assign ALUCont3 = 1'b0;
endmodule
