// Logisim project RegisterGroup_Design.circ as structural Verilog: 4 circuits, main circuit Clocked_D_FlipFlop
module Clocked_D_FlipFlop (
  input  D,
  input  Clock,
  output Q,
  output Q_Bar
);

  wire nand_1_out, nand_2_out, nand_3_out, nand_4_out, nand_5_out, nand_6_out, not_1_out, not_2_out;

  nand nand_1 (nand_1_out, D, Clock);
  nand nand_2 (nand_2_out, Clock, not_1_out);
  not not_1 (not_1_out, D);
  nand nand_3 (nand_3_out, nand_1_out, nand_4_out);
  nand nand_4 (nand_4_out, nand_3_out, nand_2_out);
  not not_2 (not_2_out, Clock);
  nand nand_5 (nand_5_out, nand_3_out, not_2_out);
  nand nand_6 (nand_6_out, not_2_out, nand_4_out);
  nand nand_7 (Q, nand_5_out, Q_Bar);
  nand nand_8 (Q_Bar, Q, nand_6_out);
endmodule

module Register32Bits (
  input  Clock,
  input  [31:0] D,
  output [31:0] Q
);

  Clocked_D_FlipFlop clocked_d_flipflop_1 (.D(D[0]), .Clock(Clock), .Q(Q[0]));  // open: Q_Bar
  Clocked_D_FlipFlop clocked_d_flipflop_2 (.D(D[1]), .Clock(Clock), .Q(Q[1]));  // open: Q_Bar
  Clocked_D_FlipFlop clocked_d_flipflop_3 (.D(D[2]), .Clock(Clock), .Q(Q[2]));  // open: Q_Bar
  Clocked_D_FlipFlop clocked_d_flipflop_4 (.D(D[3]), .Clock(Clock), .Q(Q[3]));  // open: Q_Bar
  Clocked_D_FlipFlop clocked_d_flipflop_5 (.D(D[4]), .Clock(Clock), .Q(Q[4]));  // open: Q_Bar
  Clocked_D_FlipFlop clocked_d_flipflop_6 (.D(D[5]), .Clock(Clock), .Q(Q[5]));  // open: Q_Bar
  Clocked_D_FlipFlop clocked_d_flipflop_7 (.D(D[6]), .Clock(Clock), .Q(Q[6]));  // open: Q_Bar
  Clocked_D_FlipFlop clocked_d_flipflop_8 (.D(D[7]), .Clock(Clock), .Q(Q[7]));  // open: Q_Bar
  Clocked_D_FlipFlop clocked_d_flipflop_9 (.D(D[8]), .Clock(Clock), .Q(Q[8]));  // open: Q_Bar
  Clocked_D_FlipFlop clocked_d_flipflop_10 (.D(D[9]), .Clock(Clock), .Q(Q[9]));  // open: Q_Bar
  Clocked_D_FlipFlop clocked_d_flipflop_11 (.D(D[10]), .Clock(Clock), .Q(Q[10]));  // open: Q_Bar
  Clocked_D_FlipFlop clocked_d_flipflop_12 (.D(D[11]), .Clock(Clock), .Q(Q[11]));  // open: Q_Bar
  Clocked_D_FlipFlop clocked_d_flipflop_13 (.D(D[12]), .Clock(Clock), .Q(Q[12]));  // open: Q_Bar
  Clocked_D_FlipFlop clocked_d_flipflop_14 (.D(D[13]), .Clock(Clock), .Q(Q[13]));  // open: Q_Bar
  Clocked_D_FlipFlop clocked_d_flipflop_15 (.D(D[14]), .Clock(Clock), .Q(Q[14]));  // open: Q_Bar
  Clocked_D_FlipFlop clocked_d_flipflop_16 (.D(D[15]), .Clock(Clock), .Q(Q[15]));  // open: Q_Bar
  Clocked_D_FlipFlop clocked_d_flipflop_17 (.D(D[16]), .Clock(Clock), .Q(Q[16]));  // open: Q_Bar
  Clocked_D_FlipFlop clocked_d_flipflop_18 (.D(D[17]), .Clock(Clock), .Q(Q[17]));  // open: Q_Bar
  Clocked_D_FlipFlop clocked_d_flipflop_19 (.D(D[18]), .Clock(Clock), .Q(Q[18]));  // open: Q_Bar
  Clocked_D_FlipFlop clocked_d_flipflop_20 (.D(D[19]), .Clock(Clock), .Q(Q[19]));  // open: Q_Bar
  Clocked_D_FlipFlop clocked_d_flipflop_21 (.D(D[20]), .Clock(Clock), .Q(Q[20]));  // open: Q_Bar
  Clocked_D_FlipFlop clocked_d_flipflop_22 (.D(D[21]), .Clock(Clock), .Q(Q[21]));  // open: Q_Bar
  Clocked_D_FlipFlop clocked_d_flipflop_23 (.D(D[22]), .Clock(Clock), .Q(Q[22]));  // open: Q_Bar
  Clocked_D_FlipFlop clocked_d_flipflop_24 (.D(D[23]), .Clock(Clock), .Q(Q[23]));  // open: Q_Bar
  Clocked_D_FlipFlop clocked_d_flipflop_25 (.D(D[24]), .Clock(Clock), .Q(Q[24]));  // open: Q_Bar
  Clocked_D_FlipFlop clocked_d_flipflop_26 (.D(D[25]), .Clock(Clock), .Q(Q[25]));  // open: Q_Bar
  Clocked_D_FlipFlop clocked_d_flipflop_27 (.D(D[26]), .Clock(Clock), .Q(Q[26]));  // open: Q_Bar
  Clocked_D_FlipFlop clocked_d_flipflop_28 (.D(D[27]), .Clock(Clock), .Q(Q[27]));  // open: Q_Bar
  Clocked_D_FlipFlop clocked_d_flipflop_29 (.D(D[28]), .Clock(Clock), .Q(Q[28]));  // open: Q_Bar
  Clocked_D_FlipFlop clocked_d_flipflop_30 (.D(D[29]), .Clock(Clock), .Q(Q[29]));  // open: Q_Bar
  Clocked_D_FlipFlop clocked_d_flipflop_31 (.D(D[30]), .Clock(Clock), .Q(Q[30]));  // open: Q_Bar
  Clocked_D_FlipFlop clocked_d_flipflop_32 (.D(D[31]), .Clock(Clock), .Q(Q[31]));  // open: Q_Bar
endmodule

module RegisterGroup (
  input  RegWrite,
  input  CLK,
  input  [4:0] ReadReg1,
  input  [4:0] WriteReg,
  input  [4:0] ReadReg2,
  input  [31:0] WriteData,
  output [31:0] ReadData1,
  output [31:0] ReadData2
);

  wire and_1_out, and_2_out, and_3_out, and_4_out, and_5_out, and_6_out, and_7_out, and_8_out, and_9_out,
       and_10_out, and_11_out, and_12_out, and_13_out, and_14_out, and_15_out, and_16_out, and_17_out,
       and_18_out, and_19_out, and_20_out, and_21_out, and_22_out, and_23_out, and_24_out, and_25_out,
       and_26_out, and_27_out, and_28_out, and_29_out, and_30_out, and_31_out, and_32_out, decoder_1_out0,
       decoder_1_out1, decoder_1_out2, decoder_1_out3, decoder_1_out4, decoder_1_out5, decoder_1_out6,
       decoder_1_out7, decoder_1_out8, decoder_1_out9, decoder_1_out10, decoder_1_out11, decoder_1_out12,
       decoder_1_out13, decoder_1_out14, decoder_1_out15, decoder_1_out16, decoder_1_out17, decoder_1_out18,
       decoder_1_out19, decoder_1_out20, decoder_1_out21, decoder_1_out22, decoder_1_out23, decoder_1_out24,
       decoder_1_out25, decoder_1_out26, decoder_1_out27, decoder_1_out28, decoder_1_out29, decoder_1_out30,
       decoder_1_out31;
  wire [31:0] register32bits_1_q, register32bits_2_q, register32bits_3_q, register32bits_4_q,
       register32bits_5_q, register32bits_6_q, register32bits_7_q, register32bits_8_q, register32bits_9_q,
       register32bits_10_q, register32bits_11_q, register32bits_12_q, register32bits_13_q,
       register32bits_14_q, register32bits_15_q, register32bits_16_q, register32bits_17_q,
       register32bits_18_q, register32bits_19_q, register32bits_20_q, register32bits_21_q,
       register32bits_22_q, register32bits_23_q, register32bits_24_q, register32bits_25_q,
       register32bits_26_q, register32bits_27_q, register32bits_28_q, register32bits_29_q,
       register32bits_30_q, register32bits_31_q, register32bits_32_q;

  Decoder #(.enable("false"), .select(5)) decoder_1 (
    .out0(decoder_1_out0), .out1(decoder_1_out1), .out2(decoder_1_out2), .out3(decoder_1_out3),
    .out4(decoder_1_out4), .out5(decoder_1_out5), .out6(decoder_1_out6), .out7(decoder_1_out7),
    .out8(decoder_1_out8), .out9(decoder_1_out9), .out10(decoder_1_out10), .out11(decoder_1_out11),
    .out12(decoder_1_out12), .out13(decoder_1_out13), .out14(decoder_1_out14), .out15(decoder_1_out15),
    .out16(decoder_1_out16), .out17(decoder_1_out17), .out18(decoder_1_out18), .out19(decoder_1_out19),
    .out20(decoder_1_out20), .out21(decoder_1_out21), .out22(decoder_1_out22), .out23(decoder_1_out23),
    .out24(decoder_1_out24), .out25(decoder_1_out25), .out26(decoder_1_out26), .out27(decoder_1_out27),
    .out28(decoder_1_out28), .out29(decoder_1_out29), .out30(decoder_1_out30), .out31(decoder_1_out31),
    .sel(WriteReg));
  and and_1 (and_1_out, CLK, RegWrite, decoder_1_out0);
  and and_2 (and_2_out, CLK, RegWrite, decoder_1_out1);
  and and_3 (and_3_out, CLK, RegWrite, decoder_1_out2);
  and and_4 (and_4_out, CLK, RegWrite, decoder_1_out3);
  and and_5 (and_5_out, CLK, RegWrite, decoder_1_out4);
  and and_6 (and_6_out, CLK, RegWrite, decoder_1_out5);
  and and_7 (and_7_out, CLK, RegWrite, decoder_1_out6);
  and and_8 (and_8_out, CLK, RegWrite, decoder_1_out7);
  and and_9 (and_9_out, CLK, RegWrite, decoder_1_out8);
  and and_10 (and_10_out, CLK, RegWrite, decoder_1_out9);
  and and_11 (and_11_out, CLK, RegWrite, decoder_1_out10);
  and and_12 (and_12_out, CLK, RegWrite, decoder_1_out11);
  and and_13 (and_13_out, CLK, RegWrite, decoder_1_out12);
  and and_14 (and_14_out, CLK, RegWrite, decoder_1_out13);
  and and_15 (and_15_out, CLK, RegWrite, decoder_1_out14);
  and and_16 (and_16_out, CLK, RegWrite, decoder_1_out15);
  and and_17 (and_17_out, CLK, RegWrite, decoder_1_out16);
  and and_18 (and_18_out, CLK, RegWrite, decoder_1_out17);
  and and_19 (and_19_out, CLK, RegWrite, decoder_1_out18);
  and and_20 (and_20_out, CLK, RegWrite, decoder_1_out19);
  and and_21 (and_21_out, CLK, RegWrite, decoder_1_out20);
  and and_22 (and_22_out, CLK, RegWrite, decoder_1_out21);
  and and_23 (and_23_out, CLK, RegWrite, decoder_1_out22);
  and and_24 (and_24_out, CLK, RegWrite, decoder_1_out23);
  and and_25 (and_25_out, CLK, RegWrite, decoder_1_out24);
  and and_26 (and_26_out, CLK, RegWrite, decoder_1_out25);
  and and_27 (and_27_out, CLK, RegWrite, decoder_1_out26);
  and and_28 (and_28_out, CLK, RegWrite, decoder_1_out27);
  and and_29 (and_29_out, CLK, RegWrite, decoder_1_out28);
  and and_30 (and_30_out, CLK, RegWrite, decoder_1_out29);
  and and_31 (and_31_out, CLK, RegWrite, decoder_1_out30);
  and and_32 (and_32_out, CLK, RegWrite, decoder_1_out31);
  Register32Bits register32bits_1 (.Clock(and_1_out), .D(WriteData), .Q(register32bits_1_q));
  Register32Bits register32bits_2 (.Clock(and_2_out), .D(WriteData), .Q(register32bits_2_q));
  Register32Bits register32bits_3 (.Clock(and_3_out), .D(WriteData), .Q(register32bits_3_q));
  Register32Bits register32bits_4 (.Clock(and_4_out), .D(WriteData), .Q(register32bits_4_q));
  Register32Bits register32bits_5 (.Clock(and_5_out), .D(WriteData), .Q(register32bits_5_q));
  Register32Bits register32bits_6 (.Clock(and_6_out), .D(WriteData), .Q(register32bits_6_q));
  Register32Bits register32bits_7 (.Clock(and_7_out), .D(WriteData), .Q(register32bits_7_q));
  Register32Bits register32bits_8 (.Clock(and_8_out), .D(WriteData), .Q(register32bits_8_q));
  Register32Bits register32bits_9 (.Clock(and_9_out), .D(WriteData), .Q(register32bits_9_q));
  Register32Bits register32bits_10 (.Clock(and_10_out), .D(WriteData), .Q(register32bits_10_q));
  Register32Bits register32bits_11 (.Clock(and_11_out), .D(WriteData), .Q(register32bits_11_q));
  Register32Bits register32bits_12 (.Clock(and_12_out), .D(WriteData), .Q(register32bits_12_q));
  Register32Bits register32bits_13 (.Clock(and_13_out), .D(WriteData), .Q(register32bits_13_q));
  Register32Bits register32bits_14 (.Clock(and_14_out), .D(WriteData), .Q(register32bits_14_q));
  Register32Bits register32bits_15 (.Clock(and_15_out), .D(WriteData), .Q(register32bits_15_q));
  Register32Bits register32bits_16 (.Clock(and_16_out), .D(WriteData), .Q(register32bits_16_q));
  Register32Bits register32bits_17 (.Clock(and_17_out), .D(WriteData), .Q(register32bits_17_q));
  Register32Bits register32bits_18 (.Clock(and_18_out), .Q(register32bits_18_q));  // open: D
  Register32Bits register32bits_19 (.Clock(and_19_out), .D(WriteData), .Q(register32bits_19_q));
  Register32Bits register32bits_20 (.Clock(and_20_out), .D(WriteData), .Q(register32bits_20_q));
  Register32Bits register32bits_21 (.Clock(and_21_out), .D(WriteData), .Q(register32bits_21_q));
  Register32Bits register32bits_22 (.Clock(and_22_out), .D(WriteData), .Q(register32bits_22_q));
  Register32Bits register32bits_23 (.Clock(and_23_out), .D(WriteData), .Q(register32bits_23_q));
  Register32Bits register32bits_24 (.Clock(and_24_out), .D(WriteData), .Q(register32bits_24_q));
  Register32Bits register32bits_25 (.Clock(and_25_out), .D(WriteData), .Q(register32bits_25_q));
  Register32Bits register32bits_26 (.Clock(and_26_out), .D(WriteData), .Q(register32bits_26_q));
  Register32Bits register32bits_27 (.Clock(and_27_out), .D(WriteData), .Q(register32bits_27_q));
  Register32Bits register32bits_28 (.Clock(and_28_out), .D(WriteData), .Q(register32bits_28_q));
  Register32Bits register32bits_29 (.Clock(and_29_out), .D(WriteData), .Q(register32bits_29_q));
  Register32Bits register32bits_30 (.Clock(and_30_out), .D(WriteData), .Q(register32bits_30_q));
  Register32Bits register32bits_31 (.Clock(and_31_out), .D(WriteData), .Q(register32bits_31_q));
  Register32Bits register32bits_32 (.Clock(and_32_out), .D(WriteData), .Q(register32bits_32_q));
  Multiplexer #(.select(5), .width(32)) multiplexer_1 (
    .in0(register32bits_1_q), .in1(register32bits_2_q), .in2(register32bits_3_q), .in3(register32bits_4_q),
    .in4(register32bits_5_q), .in5(register32bits_6_q), .in6(register32bits_7_q), .in7(register32bits_8_q),
    .in8(register32bits_9_q), .in9(register32bits_10_q), .in10(register32bits_11_q),
    .in11(register32bits_12_q), .in12(register32bits_13_q), .in13(register32bits_14_q),
    .in14(register32bits_15_q), .in15(register32bits_16_q), .in16(register32bits_17_q),
    .in17(register32bits_18_q), .in18(register32bits_19_q), .in19(register32bits_20_q),
    .in20(register32bits_21_q), .in21(register32bits_22_q), .in22(register32bits_23_q),
    .in23(register32bits_24_q), .in24(register32bits_25_q), .in25(register32bits_26_q),
    .in26(register32bits_27_q), .in27(register32bits_28_q), .in28(register32bits_29_q),
    .in29(register32bits_30_q), .in30(register32bits_31_q), .in31(register32bits_32_q), .out(ReadData1),
    .sel(ReadReg1));
  Multiplexer #(.select(5), .width(32)) multiplexer_2 (
    .in0(register32bits_1_q), .in1(register32bits_2_q), .in2(register32bits_3_q), .in3(register32bits_4_q),
    .in4(register32bits_5_q), .in5(register32bits_6_q), .in6(register32bits_7_q), .in7(register32bits_8_q),
    .in8(register32bits_9_q), .in9(register32bits_10_q), .in10(register32bits_11_q),
    .in11(register32bits_12_q), .in12(register32bits_13_q), .in13(register32bits_14_q),
    .in14(register32bits_15_q), .in15(register32bits_16_q), .in16(register32bits_17_q),
    .in17(register32bits_18_q), .in18(register32bits_19_q), .in19(register32bits_20_q),
    .in20(register32bits_21_q), .in21(register32bits_22_q), .in22(register32bits_23_q),
    .in23(register32bits_24_q), .in24(register32bits_25_q), .in25(register32bits_26_q),
    .in26(register32bits_27_q), .in27(register32bits_28_q), .in28(register32bits_29_q),
    .in29(register32bits_30_q), .in30(register32bits_31_q), .in31(register32bits_32_q), .out(ReadData2),
    .sel(ReadReg2));
endmodule

module RegisterTest (
  input  in_1,
  input  in_2,
  input  [4:0] in_3,
  input  [4:0] in_4,
  input  [4:0] in_5,
  input  [31:0] in_6,
  output [31:0] out_7,
  output [31:0] out_8
);

  RegisterGroup registergroup_1 (
    .RegWrite(in_1), .CLK(in_2), .ReadReg1(in_3), .WriteReg(in_4), .ReadReg2(in_5), .WriteData(in_6),
    .ReadData1(out_7), .ReadData2(out_8));
endmodule
